# Fritzing sketch initial_alarm (saved by Fritzing 0.9.2b)
breadboards: 1

parts:
  Componente1 = Modulo Rele
  Componente2 = Arduino Uno (Rev3)
  SP1 = SPEAKER [package=pcb_mount_speaker]
  U2 = Mystery Part - 4 pins [chip_label=? package=THT]
  Lhi1 = LHi958 [package=to-39]
  Lhi2 = LHi958 [package=to-39]
  S1 = Pushbutton [package="[THT]"]
  LED1 = smd LED [color="Green (555nm)" package="0603 [SMD]"]
  LED2 = smd LED [color="Red (633nm)" package="0603 [SMD]"]
  R1 = Resistor [tolerance=±5% resistance=330 package="2010 [SMD]"]
  R2 = Resistor [tolerance=±5% resistance=330 package="2010 [SMD]"]
  R3 = Resistor [tolerance=±5% resistance=1k package="2010 [SMD]"]
  R4 = Resistor [tolerance=±5% resistance=1k package="2010 [SMD]"]

nets:
  N1: Componente1.A0, Componente2.GND, U2.Ground, S1.Pin_3, S1.Pin_4, R1.Pin_0, R2.Pin_0, R3.Pin_1, R4.Pin_1
  5V: Componente1.pin_1, Componente2.5V, U2.5V, Lhi1.D, Lhi2.D
  N2: Componente1.pin_2, Componente2.D8
  N3: Componente1.pin_3, SP1.-
  N4: Componente2.D9_PWM, LED1.anode
  N5: Componente2.D10_PWM/SS, LED2.anode
  N6: Componente2.D2, U2.Signal
  N7: Componente2.D3_PWM, Lhi1.S, R3.Pin_0
  N8: Componente2.D4, Lhi2.S, R4.Pin_0
  N9: Componente2.D5_PWM, S1.Pin_1, S1.Pin_2
  N10: LED1.cathode, R1.Pin_1
  N11: LED2.cathode, R2.Pin_1

custom parts:
  Modulo Rele: The Arduino Uno is a microcontroller board based on the ATmega328 (datasheet). It has 14 digital input/output pins (of which 6 can be used as PWM outputs), 6 analog inputs, a 16 MHz ceramic resonator, a USB connection, a power jack, an ICSP header, and a reset button. It contains everything needed to support the microcontroller; simply connect it to a computer with a USB cable or power it with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
  Mystery Part - 4 pins: A dummy, proxy, ersatz, stand-in part for whatever you want. With 4 pins on a 100 mil inline pin header footprint.
