# Fritzing sketch ligacao_rele (saved by Fritzing 0.9.2b)
breadboards: 1

parts:
  Componente1 = Modulo Rele
  Componente2 = Arduino Uno (Rev3)
  SP1 = SPEAKER [package=pcb_mount_speaker]

nets:
  N1: Componente1.A0, Componente2.GND
  N2: Componente1.pin_1, Componente2.5V
  N3: Componente1.pin_2, Componente2.D2
  N4: Componente1.pin_3, SP1.-

custom parts:
  Modulo Rele: The Arduino Uno is a microcontroller board based on the ATmega328 (datasheet). It has 14 digital input/output pins (of which 6 can be used as PWM outputs), 6 analog inputs, a 16 MHz ceramic resonator, a USB connection, a power jack, an ICSP header, and a reset button. It contains everything needed to support the microcontroller; simply connect it to a computer with a USB cable or power it with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
